# Fritzing sketch ESP8266_I2C_EEPROM (saved by Fritzing 0.9.3b)
breadboards: 1

parts:
  Adafruit_HUZZAH_ESP8266_Breakout = Adafruit HUZZAH ESP8266 Breakout [part_number=2471]
  C1 = Ceramic Capacitor [capacitance=100nF package="100 mil [THT, multilayer]"]
  C2 = Ceramic Capacitor [capacitance=100nF package="100 mil [THT, multilayer]"]
  U2 = EEPROM-I2C [package=so08]

nets:
  N1: Adafruit_HUZZAH_ESP8266_Breakout.GND, C1.0, C2.1, U2.A0, U2.A1, U2.A2, U2.WP
  N2: Adafruit_HUZZAH_ESP8266_Breakout.#5, U2.SCL
  N3: Adafruit_HUZZAH_ESP8266_Breakout.#4, U2.SDA
  N4: Adafruit_HUZZAH_ESP8266_Breakout.3V, C2.0

notes:
  ESP8266 with EEPROM I2C Interface
  Generic SOIC/DIP Package
  @PatternAgents
